# Fritzing sketch TrafficControllerScheme (saved by Fritzing 0.9.3b)
circuit board: 8.46667cm x 5.64444cm
breadboards: 1

parts:
  Part1 = Arduino Uno (Rev3)
  LED1 = LED - 5mm [color="Red (633nm)" package="5 mm [THT]"]
  LED2 = LED - 5mm [color="Yellow (585nm)" package="5 mm [THT]"]
  LED3 = LED - 5mm [color="Green (560nm)" package="5 mm [THT]"]
  LED4 = LED - 5mm [color="Red (633nm)" package="5 mm [THT]"]
  LED5 = smd LED [color="Green (570nm)" package="0603 [SMD]"]
  R1 = Resistor [tolerance=±5% resistance=220 package=THT]
  R3 = Resistor [tolerance=±5% resistance=220 package=THT]
  R4 = Resistor [tolerance=±5% resistance=220 package=THT]
  R5 = Resistor [tolerance=±5% resistance=220 package=THT]
  R6 = Resistor [tolerance=±5% resistance=220 package=THT]

nets:
  N1: Part1.D11_PWM/MOSI, LED3.anode
  N2: Part1.D12/MISO, LED2.anode
  N3: Part1.D13/SCK, LED1.anode
  N4: Part1.D2, LED4.anode
  N5: Part1.D3_PWM, LED5.anode
  N6: Part1.GND, R1.Pin_1, R3.Pin_1, R4.Pin_1, R5.Pin_1, R6.Pin_1
  N7: LED1.cathode, R1.Pin_0
  N8: LED2.cathode, R3.Pin_0
  N9: LED3.cathode, R4.Pin_0
  N10: LED4.cathode, R5.Pin_0
  N11: LED5.cathode, R6.Pin_0

// code stored in the sketch: led_yakma.ino
#define wayLedRed 13
#define wayLedYellow 12
#define wayLedGreen 11

#define crossWalkGreen 3
#define crossWalkRed 2


void setup()
{
  pinMode(wayLedRed, OUTPUT);
  pinMode(wayLedYellow, OUTPUT);
  pinMode(wayLedGreen, OUTPUT);
  pinMode(crossWalkGreen, OUTPUT);
  pinMode(crossWalkRed, OUTPUT);
}


void changeLights(uint8_t redWay, uint8_t yellowWay, uint8_t greenWay, uint8_t redcrossWalk, uint8_t greencrossWalk, int second)
{
  digitalWrite(wayLedRed, redWay);
  digitalWrite(wayLedYellow, yellowWay);
  digitalWrite(wayLedGreen, greenWay);
  digitalWrite(crossWalkGreen, greencrossWalk);
  digitalWrite(crossWalkRed, redcrossWalk);
  delay(second);
}


void loop()
{
  changeLights(HIGH, LOW, LOW, LOW, HIGH, 8000);  
  changeLights(LOW, HIGH, LOW, HIGH, LOW, 2000);
  changeLights(LOW, LOW, HIGH, HIGH, LOW, 6000);
  changeLights(LOW, HIGH, LOW, HIGH, LOW, 2000);
  changeLights(HIGH, LOW, LOW, HIGH, LOW, 2000);
}
